# Fritzing sketch eletricSchema (saved by Fritzing 0.9.3b)
breadboards: 1

parts:
  S1 = H-Bridge with L298N
  Part1 = Arduino Uno (Rev3)
  T1 = LM35 Temperature Sensor [package="TO92 [THT]"]
  M2 = Stepper Motor - Bipolar
  R1 = PHOTOCELL [package=photocell]
  R2 = Resistor [tolerance=±5% resistance=10k package="1206 [SMD]"]
  LED1 = LED - 5mm [color="Red (633nm)" package="5 mm [THT]"]
  R3 = Resistor [tolerance=±5% resistance=220 package="0603 [SMD]"]
  U3 = RELAY [package=relay-jzc]
  U4 = RELAY [package=relay-jzc]
  U5 = RELAY [package=relay-jzc]  # not connected
  U6 = RELAY [package=relay-jzc]
  M3 = DC Motor
  S4 = SPST Switch [package=switch-spdt_kit]
  S5 = SPST Switch [package=switch-spdt]
  hc-sr1 = hc-sr04  # not connected
  hc-sr2 = hc-sr04  # not connected
  U7 = RELAY [package=relay-jzc]  # not connected

nets:
  GND: S1.GND, Part1.GND, T1.GND, R2.Pin_0, LED1.anode, U6.COIL1
  5V: S1.5V, S1.ENA, S1.ENB, Part1.5V, T1.+Vs, R1.P$2, U6.MAIN, S4.S, S5.S
  N1: S1.IN1, Part1.D2
  N2: S1.IN2, Part1.D3_PWM
  N3: S1.IN3, Part1.D4
  N4: S1.IN4, Part1.D5_PWM
  N5: S1.M1-01, M2.C
  N6: S1.M1-02, M2.A
  N7: S1.M2-01, M2.D
  N8: S1.M2-02, M2.B
  N9: Part1.A0, T1.Vout
  N10: Part1.A1, R1.P$1, R2.Pin_1
  N11: Part1.A2, S4.O
  N12: Part1.A3, S5.O
  N13: Part1.D1/TX, R3.Pin_1
  N14: LED1.cathode, R3.Pin_0
  N15: U3.NC, U4.NC
  N16: U3.NO, M3.pin_1
  N17: U6.NC, M3.pin_2

custom parts:
  H-Bridge with L298N: h-bridge
